# Fritzing sketch mp3_çalar (saved by Fritzing 0.9.5d)
breadboards: 1

parts:
  A1 = Pcm5102A module
  TP1 = TP4056 [chip_label=TP4056 package="DIP (Dual Inline) [THT]"]
  MOD1 = MT3608 Boost No usb
  A2 = ESP32-S3 devkit 1
  U1 = WS2812 RGB LED strip
  U2 = LIPO-2000mAh [package=lipo-2000]
  LCD1 = 2.8" SPI TFT Module [part_number=MSP2807]

nets (from the schematic view):
  N1: A1.Pin_1, A1.Pin_5, TP1.pin3, MOD1.IN_(-), MOD1.OUT_(-), A2.Pin_1, A2.Pin_42, U1.GND, LCD1.pin2
  N2: A1.Pin_2, A2.Pin_4
  N3: A1.Pin_3, A2.Pin_5
  N4: A1.Pin_6, MOD1.OUT_(+), A2.Pin_22, U1.VCC#1, LCD1.pin1
  N5: TP1.pin4, U2.+
  N6: TP1.pin5, U2.-
  N7: TP1.pin6, MOD1.IN_(+), U1.DOUT
  N8: A2.Pin_11, U1.DIN
  N9: A2.Pin_17, LCD1.pin18
  N10: A2.Pin_18, LCD1.pin17
  N11: A2.Pin_19, LCD1.pin16
  N12: A2.Pin_20, LCD1.pin15
  N13: A2.Pin_24, LCD1.pin14
  N14: A2.Pin_25, LCD1.pin13
  N15: A2.Pin_26, LCD1.pin12
  N16: A2.Pin_27, LCD1.pin11
  N17: A2.Pin_30, LCD1.pin10
  N18: A2.Pin_31, LCD1.pin9
  N19: A2.Pin_32, LCD1.pin8
  N20: A2.Pin_33, LCD1.pin7
  N21: A2.Pin_34, LCD1.pin6
  N22: A2.Pin_35, LCD1.pin5
  N23: A2.Pin_36, LCD1.pin4
  N24: A2.Pin_37, LCD1.pin3

custom parts:
  Pcm5102A module: Interface I2S PCM5102A DAC Decoder GY-PCM5102 I2S Player Module for Raspberry Pi pHAT Format Board Digital PCM5102 Audio Board.
  TP4056: A DIP stand-in part for whatever IC you want. With 6 pins on a 300mil dual inline package (DIP) footprint.
  MT3608 Boost No usb: Chip- MT3608 / B6289 DC to DC step up, power booster module. With adjustable output voltage. Current- 2A . || Input voltage- 2V-24V || Output voltage- 5V-28V Input interface- Inversed polarity- NO. || Led indicator- No.
  ESP32-S3 devkit 1: ESP32-S3-DevKitC-1 Development Board BT 2.4G Wifi Module for Arduino 8MB PSRAM 16MB FLASH N16R8 42Pin CH340C Type-C ESP32 S3.
  WS2812 RGB LED strip: WS2812 strip
  2.8" SPI TFT Module: A generic 2.8 inch LCD TFT 320x240 display with touchscreen and SD card slot. Uses the ILI9341 controller, like the Adafruit displays of this size uses.
